// Logisim project mapa.circ as structural Verilog
module mapa (
  input  B3,
  input  B2,
  input  B1,
  input  B0,
  output a,
  output b,
  output c,
  output d,
  output e,
  output f,
  output g
);

  wire and_1_out, and_2_out, and_3_out, and_4_out, and_5_out, and_6_out, and_7_out, and_8_out, and_9_out,
       and_10_out, and_11_out, and_12_out, and_13_out, and_14_out, and_15_out, and_16_out, and_17_out,
       and_18_out, and_19_out, and_20_out, and_21_out, and_22_out, and_23_out, and_24_out, and_25_out,
       and_26_out, and_27_out, and_28_out, not_1_out, not_2_out, not_3_out, not_4_out, not_5_out, not_6_out,
       not_7_out, not_8_out, not_9_out, not_10_out, not_11_out, not_12_out, not_13_out, not_14_out,
       not_15_out, not_16_out, not_17_out, not_18_out, not_19_out, not_20_out, not_21_out, not_22_out,
       not_23_out, not_24_out, not_25_out, not_26_out, not_27_out, not_28_out, not_29_out, not_30_out,
       not_31_out, not_32_out, not_33_out, not_34_out;

  not not_1 (not_1_out, B3);
  and and_1 (and_1_out, not_1_out, not_2_out);
  not not_2 (not_2_out, B0);
  and and_2 (and_2_out, B1, not_3_out);
  not not_3 (not_3_out, B0);
  not not_4 (not_4_out, B3);
  and and_3 (and_3_out, not_4_out, B2);
  and and_4 (and_4_out, B3, not_5_out, B0);
  not not_5 (not_5_out, B2);
  and and_5 (and_5_out, B3, not_6_out, B0);
  not not_6 (not_6_out, B1);
  not not_7 (not_7_out, B3);
  and and_6 (and_6_out, not_7_out, not_8_out);
  not not_8 (not_8_out, B1);
  not not_9 (not_9_out, B3);
  and and_7 (and_7_out, not_9_out, not_10_out);
  not not_10 (not_10_out, B0);
  not not_11 (not_11_out, B1);
  and and_8 (and_8_out, not_11_out, not_12_out);
  not not_12 (not_12_out, B0);
  and and_9 (and_9_out, B3, B1, B0);
  and and_10 (and_10_out, B3, B2);
  not not_13 (not_13_out, B3);
  and and_11 (and_11_out, not_13_out, not_14_out);
  not not_14 (not_14_out, B1);
  not not_15 (not_15_out, B3);
  and and_12 (and_12_out, not_15_out, not_16_out);
  not not_16 (not_16_out, B0);
  not not_17 (not_17_out, B1);
  and and_13 (and_13_out, not_17_out, not_18_out);
  not not_18 (not_18_out, B0);
  and and_14 (and_14_out, B3, B2);
  not not_19 (not_19_out, B2);
  and and_15 (and_15_out, not_19_out, not_20_out);
  not not_20 (not_20_out, B0);
  not not_21 (not_21_out, B3);
  and and_16 (and_16_out, not_21_out, B2, B1);
  and and_17 (and_17_out, B3, not_22_out);
  not not_22 (not_22_out, B2);
  and and_18 (and_18_out, B3, not_23_out);
  not not_23 (not_23_out, B0);
  not not_24 (not_24_out, B3);
  and and_19 (and_19_out, not_24_out, not_25_out);
  not not_25 (not_25_out, B1);
  not not_26 (not_26_out, B1);
  and and_20 (and_20_out, not_26_out, not_27_out);
  not not_27 (not_27_out, B0);
  and and_21 (and_21_out, B3, not_28_out, not_29_out);
  not not_28 (not_28_out, B2);
  not not_29 (not_29_out, B0);
  and and_22 (and_22_out, B3, B2, B0);
  not not_30 (not_30_out, B3);
  and and_23 (and_23_out, not_30_out, not_31_out);
  not not_31 (not_31_out, B1);
  not not_32 (not_32_out, B1);
  and and_24 (and_24_out, not_32_out, not_33_out);
  not not_33 (not_33_out, B0);
  and and_25 (and_25_out, B3, not_34_out, B1);
  not not_34 (not_34_out, B2);
  and and_26 (and_26_out, B3, B2, B0);
  and and_27 (and_27_out, B1, B0);
  and and_28 (and_28_out, B2, B0);
  or or_1 (a, and_1_out, and_2_out, and_3_out, and_4_out, and_5_out);
  or or_2 (b, and_6_out, and_7_out, and_8_out, and_9_out, and_10_out);
  or or_3 (c, and_11_out, and_12_out, and_13_out, and_14_out);
  or or_4 (d, and_15_out, and_16_out, and_17_out, and_18_out);
  or or_5 (e, and_19_out, and_20_out, and_21_out, and_22_out);
  or or_6 (f, and_23_out, and_24_out, and_25_out, and_26_out);
  or or_7 (g, and_27_out, and_28_out);
endmodule

module a (
  input  B3,
  input  B2,
  input  B1,
  input  B0,
  output a,
  output b,
  output c,
  output d,
  output e,
  output f,
  output g
);

  wire and_1_out, and_2_out, and_3_out, and_4_out, and_5_out, and_6_out, and_7_out, and_8_out, and_9_out,
       and_10_out, and_11_out, and_12_out, and_13_out, and_14_out, and_15_out, and_16_out, and_17_out,
       and_18_out, and_19_out, and_20_out, and_21_out, and_22_out, and_23_out, and_24_out, and_25_out,
       and_26_out, and_27_out, and_28_out, not_1_out, not_2_out, not_3_out, not_4_out, not_5_out, not_6_out,
       not_7_out, not_8_out, not_9_out, not_10_out, not_11_out, not_12_out, not_13_out, not_14_out,
       not_15_out, not_16_out, not_17_out, not_18_out, not_19_out, not_20_out, not_21_out, not_22_out,
       not_23_out, not_24_out, not_25_out, not_26_out, not_27_out, not_28_out, not_29_out, not_30_out,
       not_31_out, not_32_out, not_33_out, not_34_out;

  not not_1 (not_1_out, B3);
  and and_1 (and_1_out, not_1_out, not_2_out);
  not not_2 (not_2_out, B0);
  and and_2 (and_2_out, B1, not_3_out);
  not not_3 (not_3_out, B0);
  not not_4 (not_4_out, B3);
  and and_3 (and_3_out, not_4_out, B2);
  not not_5 (not_5_out, B2);
  and and_4 (and_4_out, B3, not_5_out, B0);
  and and_5 (and_5_out, B3, not_6_out, B0);
  not not_6 (not_6_out, B1);
  not not_7 (not_7_out, B3);
  and and_6 (and_6_out, not_7_out, not_8_out);
  not not_8 (not_8_out, B1);
  not not_9 (not_9_out, B3);
  and and_7 (and_7_out, not_9_out, not_10_out);
  not not_10 (not_10_out, B0);
  not not_11 (not_11_out, B1);
  and and_8 (and_8_out, not_11_out, not_12_out);
  not not_12 (not_12_out, B0);
  and and_9 (and_9_out, B3, B1, B0);
  and and_10 (and_10_out, B3, B2);
  not not_13 (not_13_out, B3);
  and and_11 (and_11_out, not_13_out, not_14_out);
  not not_14 (not_14_out, B1);
  not not_15 (not_15_out, B3);
  and and_12 (and_12_out, not_15_out, not_16_out);
  not not_16 (not_16_out, B0);
  not not_17 (not_17_out, B1);
  and and_13 (and_13_out, not_17_out, not_18_out);
  not not_18 (not_18_out, B0);
  and and_14 (and_14_out, B3, B2);
  not not_19 (not_19_out, B2);
  and and_15 (and_15_out, not_19_out, not_20_out);
  not not_20 (not_20_out, B0);
  not not_21 (not_21_out, B3);
  and and_16 (and_16_out, not_21_out, B2, B1);
  and and_17 (and_17_out, B3, not_22_out);
  not not_22 (not_22_out, B2);
  and and_18 (and_18_out, B3, not_23_out);
  not not_23 (not_23_out, B0);
  not not_24 (not_24_out, B3);
  and and_19 (and_19_out, not_24_out, not_25_out);
  not not_25 (not_25_out, B1);
  not not_26 (not_26_out, B1);
  and and_20 (and_20_out, not_26_out, not_27_out);
  not not_27 (not_27_out, B0);
  not not_28 (not_28_out, B2);
  and and_21 (and_21_out, B3, not_28_out, not_29_out);
  not not_29 (not_29_out, B0);
  and and_22 (and_22_out, B3, B2, B0);
  not not_30 (not_30_out, B3);
  and and_23 (and_23_out, not_30_out, not_31_out);
  not not_31 (not_31_out, B1);
  not not_32 (not_32_out, B1);
  and and_24 (and_24_out, not_32_out, not_33_out);
  not not_33 (not_33_out, B0);
  and and_25 (and_25_out, B3, not_34_out, B1);
  not not_34 (not_34_out, B2);
  and and_26 (and_26_out, B3, B2, B0);
  and and_27 (and_27_out, B1, B0);
  and and_28 (and_28_out, B2, B0);
  or or_1 (a, and_1_out, and_2_out, and_3_out, and_4_out, and_5_out);
  or or_2 (b, and_6_out, and_7_out, and_8_out, and_9_out, and_10_out);
  or or_3 (c, and_11_out, and_12_out, and_13_out, and_14_out);
  or or_4 (d, and_15_out, and_16_out, and_17_out, and_18_out);
  or or_5 (e, and_19_out, and_20_out, and_21_out, and_22_out);
  or or_6 (f, and_23_out, and_24_out, and_25_out, and_26_out);
  or or_7 (g, and_27_out, and_28_out);
endmodule
