// Logisim project secuencia.circ as structural Verilog: 4 circuits, main circuit main
module main (
);

  wire clock_1_out, flip_flops_1_out_6, flip_flops_1_out_7, flip_flops_1_out_8, flip_flops_1_out_9,
       logica_de_estados_1_ffde0, logica_de_estados_1_ffde1, logica_de_estados_1_ffde2,
       logica_de_estados_1_ffde3, logica_de_salida_1_out_5, logica_de_salida_1_out_6,
       logica_de_salida_1_out_7, logica_de_salida_1_out_8, logica_de_salida_1_out_9,
       logica_de_salida_1_out_10, logica_de_salida_1_out_11;

  Logica_de_estados logica_de_estados_1 (
    .E3(flip_flops_1_out_9), .E2(flip_flops_1_out_8), .E1(flip_flops_1_out_7), .E0(flip_flops_1_out_6),
    .FFDE0(logica_de_estados_1_ffde0), .FFDE1(logica_de_estados_1_ffde1), .FFDE2(logica_de_estados_1_ffde2),
    .FFDE3(logica_de_estados_1_ffde3));
  Clock clock_1 (.out(clock_1_out));
  Flip_Flops flip_flops_1 (
    .in_1(clock_1_out), .in_2(logica_de_estados_1_ffde0), .in_3(logica_de_estados_1_ffde1),
    .in_4(logica_de_estados_1_ffde2), .in_5(logica_de_estados_1_ffde3), .out_6(flip_flops_1_out_6),
    .out_7(flip_flops_1_out_7), .out_8(flip_flops_1_out_8), .out_9(flip_flops_1_out_9));
  Logica_de_salida logica_de_salida_1 (
    .in_1(flip_flops_1_out_9), .in_2(flip_flops_1_out_8), .in_3(flip_flops_1_out_7),
    .in_4(flip_flops_1_out_6), .out_5(logica_de_salida_1_out_5), .out_6(logica_de_salida_1_out_6),
    .out_7(logica_de_salida_1_out_7), .out_8(logica_de_salida_1_out_8), .out_9(logica_de_salida_1_out_9),
    .out_10(logica_de_salida_1_out_10), .out_11(logica_de_salida_1_out_11));
  _7_Segment_Display u_7_segment_display_1 (
    .g(logica_de_salida_1_out_11), .f(logica_de_salida_1_out_10), .a(logica_de_salida_1_out_5),
    .b(logica_de_salida_1_out_6), .e(logica_de_salida_1_out_9), .d(logica_de_salida_1_out_8),
    .c(logica_de_salida_1_out_7));  // open: dp
endmodule

module Logica_de_estados (
  input  E3,
  input  E2,
  input  E1,
  input  E0,
  output FFDE0,
  output FFDE1,
  output FFDE2,
  output FFDE3
);

  wire and_1_out, and_2_out, and_3_out, and_4_out, and_5_out, and_6_out, and_7_out, and_8_out, and_9_out,
       not_2_out, not_3_out, not_4_out, not_5_out, not_6_out, not_7_out, not_8_out, not_9_out, not_10_out;

  not not_1 (FFDE0, E0);
  not not_2 (not_2_out, E1);
  not not_3 (not_3_out, E0);
  not not_4 (not_4_out, E1);
  not not_5 (not_5_out, E2);
  not not_6 (not_6_out, E0);
  not not_7 (not_7_out, E2);
  not not_8 (not_8_out, E1);
  not not_9 (not_9_out, E0);
  not not_10 (not_10_out, E3);
  and and_1 (and_1_out, not_2_out, E0);
  and and_2 (and_2_out, E1, not_3_out);
  and and_3 (and_3_out, E2, not_4_out);
  and and_4 (and_4_out, not_5_out, E0, E1);
  and and_5 (and_5_out, E2, not_6_out);
  and and_6 (and_6_out, E3, not_7_out);
  and and_7 (and_7_out, E3, not_8_out);
  and and_8 (and_8_out, E3, not_9_out);
  and and_9 (and_9_out, not_10_out, E0, E1, E2);
  or or_1 (FFDE1, and_1_out, and_2_out);
  or or_2 (FFDE2, and_3_out, and_4_out, and_5_out);
  or or_3 (FFDE3, and_6_out, and_7_out, and_8_out, and_9_out);
endmodule

module Flip_Flops (
  input  in_1,
  input  in_2,
  input  in_3,
  input  in_4,
  input  in_5,
  output out_6,
  output out_7,
  output out_8,
  output out_9
);

  D_Flip_Flop d_ff_1 (.clk(in_1), .D(in_2), .Q(out_6), .en(1'b1));  // open: Qn, preset, reset
  D_Flip_Flop d_ff_2 (.clk(in_1), .D(in_3), .Q(out_7), .en(1'b1));  // open: Qn, preset, reset
  D_Flip_Flop d_ff_3 (.clk(in_1), .D(in_4), .Q(out_8), .en(1'b1));  // open: Qn, preset, reset
  D_Flip_Flop d_ff_4 (.clk(in_1), .D(in_5), .Q(out_9), .en(1'b1));  // open: Qn, preset, reset
endmodule

module Logica_de_salida (
  input  in_1,
  input  in_2,
  input  in_3,
  input  in_4,
  output out_5,
  output out_6,
  output out_7,
  output out_8,
  output out_9,
  output out_10,
  output out_11
);

  wire and_1_out, and_2_out, and_3_out, and_4_out, and_5_out, and_6_out, and_7_out, and_8_out, and_9_out,
       and_10_out, and_11_out, and_12_out, and_13_out, and_14_out, and_15_out, and_16_out, and_17_out,
       and_18_out, and_19_out, and_20_out, and_21_out, and_22_out, and_23_out, and_24_out, and_25_out,
       and_26_out, and_27_out, and_28_out, and_29_out, and_30_out, not_1_out, not_2_out, not_3_out,
       not_4_out, not_5_out, not_6_out, not_7_out, not_8_out, not_9_out, not_10_out, not_11_out, not_12_out,
       not_13_out, not_14_out, not_15_out, not_16_out, not_17_out, not_18_out, not_19_out, not_20_out,
       not_21_out, not_22_out, not_23_out, not_24_out, not_25_out, not_26_out, not_27_out, not_28_out,
       not_29_out, not_30_out, not_31_out, not_32_out;

  not not_1 (not_1_out, in_2);
  not not_2 (not_2_out, in_1);
  not not_3 (not_3_out, in_1);
  not not_4 (not_4_out, in_4);
  not not_5 (not_5_out, in_4);
  not not_6 (not_6_out, in_3);
  not not_7 (not_7_out, in_4);
  not not_8 (not_8_out, in_3);
  not not_9 (not_9_out, in_4);
  not not_10 (not_10_out, in_3);
  not not_11 (not_11_out, in_1);
  not not_12 (not_12_out, in_2);
  not not_13 (not_13_out, in_3);
  not not_14 (not_14_out, in_4);
  not not_15 (not_15_out, in_1);
  not not_16 (not_16_out, in_2);
  not not_17 (not_17_out, in_2);
  not not_18 (not_18_out, in_1);
  not not_19 (not_19_out, in_2);
  not not_20 (not_20_out, in_3);
  not not_21 (not_21_out, in_1);
  not not_22 (not_22_out, in_4);
  not not_23 (not_23_out, in_3);
  not not_24 (not_24_out, in_1);
  not not_25 (not_25_out, in_2);
  not not_26 (not_26_out, in_4);
  not not_27 (not_27_out, in_1);
  not not_28 (not_28_out, in_4);
  not not_29 (not_29_out, in_3);
  not not_30 (not_30_out, in_1);
  not not_31 (not_31_out, in_4);
  not not_32 (not_32_out, in_2);
  and and_1 (and_1_out, in_3, not_1_out, not_2_out);
  and and_2 (and_2_out, in_2, not_3_out, in_4);
  and and_3 (and_3_out, in_2, not_4_out, in_1);
  and and_4 (and_4_out, in_3, not_5_out, in_1);
  and and_5 (and_5_out, in_2, not_6_out, not_7_out);
  and and_6 (and_6_out, in_4, in_3);
  and and_7 (and_7_out, in_3, in_2, in_1);
  and and_8 (and_8_out, in_2, not_8_out, not_9_out);
  and and_9 (and_9_out, in_4, not_10_out, not_11_out);
  and and_10 (and_10_out, in_4, in_3, in_2);
  and and_11 (and_11_out, in_4, in_3, in_1);
  and and_12 (and_12_out, in_3, in_2, in_1);
  and and_13 (and_13_out, not_12_out, in_1);
  and and_14 (and_14_out, in_4, not_13_out, in_2);
  and and_15 (and_15_out, in_3, not_14_out, not_15_out, in_2);
  and and_16 (and_16_out, in_4, in_3, not_16_out);
  and and_17 (and_17_out, not_17_out, not_18_out);
  and and_18 (and_18_out, not_19_out, in_1);
  and and_19 (and_19_out, not_20_out, in_1);
  and and_20 (and_20_out, in_4, in_3);
  and and_21 (and_21_out, in_3, not_21_out);
  and and_22 (and_22_out, not_22_out, not_23_out);
  and and_23 (and_23_out, in_2, not_24_out);
  and and_24 (and_24_out, not_25_out, in_1);
  and and_25 (and_25_out, not_26_out, not_27_out);
  and and_26 (and_26_out, in_4, in_1);
  and and_27 (and_27_out, not_28_out, not_29_out, in_2);
  and and_28 (and_28_out, in_4, not_30_out);
  and and_29 (and_29_out, in_4, in_3, in_2);
  and and_30 (and_30_out, not_31_out, in_3, not_32_out);
  or or_1 (out_5, and_1_out, and_2_out, and_3_out, and_4_out);
  or or_2 (out_6, and_5_out, and_6_out, and_7_out);
  or or_3 (out_7, and_8_out, and_9_out, and_10_out, and_11_out, and_12_out);
  or or_4 (out_8, and_13_out, and_14_out, and_15_out, and_16_out);
  or or_5 (out_9, and_17_out, and_18_out, and_19_out, and_20_out, and_21_out);
  or or_6 (out_10, and_22_out, and_23_out, and_24_out, and_25_out, and_26_out);
  or or_7 (out_11, and_27_out, and_28_out, and_29_out, and_30_out);
endmodule
